// Logisim project exam.circ as structural Verilog: 16 circuits, main circuit main
module main (
  output [4:0] out_1
);

  wire and_1_out, main_control_1_alusrc, main_control_1_branch, main_control_1_mem_read,
       main_control_1_mem_write, main_control_1_memtoreg, main_control_1_regdest, main_control_1_regwrite,
       n32_bit_alu_1_zero;
  wire [1:0] main_control_1_aluop0;
  wire [3:0] alu_control_1_aluctrl_4;
  wire [4:0] memory_address_2_out_5, multiplexer_1_out;
  wire [31:0] adder_1_out, adder_2_out, data_memory_1_read_data_32, left_shift_2_1_data__32_2,
       multiplexer_2_out, multiplexer_3_out, multiplexer_4_out, n32_bit_alu_1_result__32,
       pc_register_1_data_out__320, reg_file_32_1_read_data_1, reg_file_32_1_read_data_2, rom_1_data,
       sign_extension_1_data__32;

  PC_Register pc_register_1 (.DATA_IN__32(multiplexer_4_out), .DATA_OUT__320(pc_register_1_data_out__320));
  Memory_Address memory_address_1 (.IN_32(pc_register_1_data_out__320), .OUT_5(out_1));
  Adder #(.width(32)) adder_1 (.a(32'h4), .b(pc_register_1_data_out__320), .out(adder_1_out));  // open: cin, cout
  ROM #(.addrWidth(5), .dataWidth(32)) rom_1 (.addr(out_1), .data(rom_1_data));  // open: sel
  Multiplexer #(.width(5)) multiplexer_1 (
    .in0(rom_1_data[20:16]), .in1(rom_1_data[15:11]), .out(multiplexer_1_out), .sel(main_control_1_regdest));  // open: en
  Main_Control main_control_1 (
    .Opcode__6(rom_1_data[31:26]), .RegDest(main_control_1_regdest), .ALUSrc(main_control_1_alusrc),
    .MemToReg(main_control_1_memtoreg), .RegWrite(main_control_1_regwrite),
    .Mem_Read(main_control_1_mem_read), .Mem_Write(main_control_1_mem_write), .Branch(main_control_1_branch),
    .ALUOp1(main_control_1_aluop0[1]), .ALUOp0(main_control_1_aluop0[0]));
  reg_file__32 reg_file_32_1 (
    .Write(main_control_1_regwrite), .Write_Register(multiplexer_1_out), .DATA__32(multiplexer_3_out),
    .Read_Data_1(reg_file_32_1_read_data_1), .Read_Data_2(reg_file_32_1_read_data_2),
    .Read_Register_1(rom_1_data[25:21]), .Read_Register_2(rom_1_data[20:16]));
  sign_extension sign_extension_1 (.DATA__16(rom_1_data[15:0]), .DATA__32(sign_extension_1_data__32));
  Multiplexer #(.width(32)) multiplexer_2 (
    .in0(reg_file_32_1_read_data_2), .in1(sign_extension_1_data__32), .out(multiplexer_2_out),
    .sel(main_control_1_alusrc));  // open: en
  Multiplexer #(.width(32)) multiplexer_3 (
    .in0(n32_bit_alu_1_result__32), .in1(data_memory_1_read_data_32), .out(multiplexer_3_out),
    .sel(main_control_1_memtoreg));  // open: en
  left_shift_2 left_shift_2_1 (.DATA__32(sign_extension_1_data__32), .DATA__32_2(left_shift_2_1_data__32_2));
  Adder #(.width(32)) adder_2 (.a(adder_1_out), .b(left_shift_2_1_data__32_2), .out(adder_2_out));  // open: cin, cout
  and and_1 (and_1_out, main_control_1_branch, n32_bit_alu_1_zero);
  _32_bit_ALU u_32_bit_alu_1 (
    .A_32(reg_file_32_1_read_data_1), .B_32(multiplexer_2_out), .Result__32(n32_bit_alu_1_result__32),
    .ZERO(n32_bit_alu_1_zero), .ALU_Control(alu_control_1_aluctrl_4));  // open: OverFlow, Cout
  ALU_Control alu_control_1 (
    .Function_6(rom_1_data[5:0]), .ALUCtrl_4(alu_control_1_aluctrl_4), .ALUOp_2(main_control_1_aluop0));
  Memory_Address memory_address_2 (.IN_32(n32_bit_alu_1_result__32), .OUT_5(memory_address_2_out_5));
  Multiplexer #(.width(32)) multiplexer_4 (
    .in0(adder_1_out), .in1(adder_2_out), .out(multiplexer_4_out), .sel(and_1_out));  // open: en
  Data_Memory data_memory_1 (
    .Address_5(memory_address_2_out_5), .Write_Data_32(reg_file_32_1_read_data_2),
    .Read_Data_32(data_memory_1_read_data_32), .Memory_Write(main_control_1_mem_write),
    .Memory_Read(main_control_1_mem_read));

  // Notes on the sheet:
  //   32
  //   /
  //   /
  //   /
  //   32
  //   32
  //   Instruction
  //   Opcode(6)
  //   Reg Dest
  //   32 BIT MIPS PROCESSOR
  //   Reg Write
  //   16
  //   /
  //   Branch
  //   Mem Read
  //   Mem Write
  //   ALU operation
  //   Mem-to-Reg
  //   ALU Src
  //   32
  //   /
  //   32
  //   /
  //   32
  //   /
  //   32
  //   /
  //   ALU OP
  //   Function
  //   32
  //   /
  //   Branch Target
  //   /
  //   32
  //   Branching
  //   Write
  //   Data
  //   PCSrc
  //   Read Data
  //   /
  //   /
  //   32
  //   32
endmodule

module _1_bit_ALU (
  input  AInvert,
  input  BInvert,
  input  Cin,
  input  [1:0] OP_2,
  input  A,
  input  Less,
  input  B,
  output Result,
  output Set,
  output OverFlow,
  output Cout
);

  wire adder_1_out, and_1_out, multiplexer_1_out, multiplexer_2_out, not_1_out, not_2_out, or_1_out;

  not not_1 (not_1_out, A);
  Multiplexer multiplexer_1 (.in0(A), .in1(not_1_out), .out(multiplexer_1_out), .sel(AInvert));  // open: en
  not not_2 (not_2_out, B);
  Multiplexer multiplexer_2 (.in0(B), .in1(not_2_out), .out(multiplexer_2_out), .sel(BInvert));  // open: en
  and and_1 (and_1_out, multiplexer_1_out, multiplexer_2_out);
  or or_1 (or_1_out, multiplexer_2_out, multiplexer_1_out);
  Adder #(.width(1)) adder_1 (.a(multiplexer_1_out), .b(multiplexer_2_out), .out(adder_1_out), .cin(Cin), .cout(Cout));
  xor xor_1 (OverFlow, Cin, Cout);
  Multiplexer #(.select(2)) multiplexer_3 (
    .in0(and_1_out), .in1(or_1_out), .in2(adder_1_out), .in3(Less), .out(Result), .sel(OP_2));  // open: en
  xor xor_2 (Set, adder_1_out, OverFlow);

  // Notes on the sheet:
  //   1-bit ALU ( AND, OR, ADD, SUB, SLT, NOR )
  //   0      0    0   0
  //   AND
  //   OR
  //   ADD
  //   SUB
  //   slt
  //   NOR
  //   Ainv Binv op1 op0
  //   0      0    0   1
  //   0      0    1   0
  //   0      1    1   0
  //   0      1    1   1
  //   1      1    0   0
endmodule

module _4_bit_ALU (
  input  AInvert,
  input  BInvert,
  input  Cin,
  input  [1:0] OP_2,
  input  [3:0] A_4,
  input  LESS,
  input  [3:0] B_4,
  input  Less_0,
  output [3:0] Result_4,
  output SET,
  output OverFolw,
  output Cout
);

  wire n1_bit_alu_1_cout, n1_bit_alu_2_cout, n1_bit_alu_3_cout;

  _1_bit_ALU u_1_bit_alu_1 (
    .A(A_4[0]), .Less(LESS), .B(B_4[0]), .Result(Result_4[0]), .AInvert(AInvert), .BInvert(BInvert),
    .Cin(Cin), .OP_2(OP_2), .Cout(n1_bit_alu_1_cout));  // open: Set, OverFlow
  _1_bit_ALU u_1_bit_alu_2 (
    .A(A_4[1]), .Less(Less_0), .B(B_4[1]), .Result(Result_4[1]), .AInvert(AInvert), .BInvert(BInvert),
    .Cin(n1_bit_alu_1_cout), .OP_2(OP_2), .Cout(n1_bit_alu_2_cout));  // open: Set, OverFlow
  _1_bit_ALU u_1_bit_alu_3 (
    .A(A_4[2]), .Less(Less_0), .B(B_4[2]), .Result(Result_4[2]), .AInvert(AInvert), .BInvert(BInvert),
    .Cin(n1_bit_alu_2_cout), .OP_2(OP_2), .Cout(n1_bit_alu_3_cout));  // open: Set, OverFlow
  _1_bit_ALU u_1_bit_alu_4 (
    .A(A_4[3]), .Less(Less_0), .B(B_4[3]), .Result(Result_4[3]), .Set(SET), .OverFlow(OverFolw),
    .AInvert(AInvert), .BInvert(BInvert), .Cin(n1_bit_alu_3_cout), .OP_2(OP_2), .Cout(Cout));

  // Notes on the sheet:
  //   4-bit ALU ( AND, OR, ADD, SUB, SLT, NOR )
  //   AND
  //   OR
  //   ADD
  //   SUB
  //   slt
  //   NOR
  //   Ainv Binv op1 op0
  //   0      0    0   0
  //   0      0    0   1
  //   0      0    1   0
  //   0      1    1   0
  //   0      1    1   1
  //   1      1    0   0
endmodule

module _16_bit_ALU (
  input  AInvert,
  input  BInvert,
  input  Cin,
  input  [1:0] OP_2,
  input  [15:0] A_16,
  input  LESS,
  input  [15:0] B_16,
  output [15:0] Result_16,
  output SET,
  output OverFlow,
  output Cout
);

  wire n4_bit_alu_1_cout, n4_bit_alu_2_cout, n4_bit_alu_3_cout;

  _4_bit_ALU u_4_bit_alu_1 (
    .A_4(A_16[3:0]), .LESS(LESS), .B_4(B_16[3:0]), .Less_0(1'b0), .Result_4(Result_16[3:0]),
    .AInvert(AInvert), .BInvert(BInvert), .Cin(Cin), .OP_2(OP_2), .Cout(n4_bit_alu_1_cout));  // open: SET, OverFolw
  _4_bit_ALU u_4_bit_alu_2 (
    .A_4(A_16[7:4]), .LESS(1'b0), .B_4(B_16[7:4]), .Less_0(1'b0), .Result_4(Result_16[7:4]),
    .AInvert(AInvert), .BInvert(BInvert), .Cin(n4_bit_alu_1_cout), .OP_2(OP_2), .Cout(n4_bit_alu_2_cout));  // open: SET, OverFolw
  _4_bit_ALU u_4_bit_alu_3 (
    .A_4(A_16[11:8]), .LESS(1'b0), .B_4(B_16[11:8]), .Less_0(1'b0), .Result_4(Result_16[11:8]),
    .AInvert(AInvert), .BInvert(BInvert), .Cin(n4_bit_alu_2_cout), .OP_2(OP_2), .Cout(n4_bit_alu_3_cout));  // open: SET, OverFolw
  _4_bit_ALU u_4_bit_alu_4 (
    .A_4(A_16[15:12]), .LESS(1'b0), .B_4(B_16[15:12]), .Less_0(1'b0), .Result_4(Result_16[15:12]), .SET(SET),
    .OverFolw(OverFlow), .AInvert(AInvert), .BInvert(BInvert), .Cin(n4_bit_alu_3_cout), .OP_2(OP_2),
    .Cout(Cout));

  // Notes on the sheet:
  //   16-bit ALU ( AND, OR, ADD, SUB, SLT, NOR )
  //   AND
  //   OR
  //   ADD
  //   SUB
  //   slt
  //   NOR
  //   Ainv Binv op1 op0
  //   0      0    0   0
  //   0      0    0   1
  //   0      0    1   0
  //   0      1    1   0
  //   0      1    1   1
  //   1      1    0   0
endmodule

module _32_bit_ALU (
  input  [3:0] ALU_Control,
  input  [31:0] A_32,
  input  [31:0] B_32,
  output [31:0] Result__32,
  output ZERO,
  output OverFlow,
  output Cout
);

  wire n16_bit_alu_1_cout, n16_bit_alu_2_set;

  _16_bit_ALU u_16_bit_alu_1 (
    .A_16(A_32[15:0]), .LESS(n16_bit_alu_2_set), .B_16(B_32[15:0]), .Result_16(Result__32[15:0]),
    .AInvert(ALU_Control[3]), .BInvert(ALU_Control[2]), .Cin(ALU_Control[2]), .OP_2(ALU_Control[1:0]),
    .Cout(n16_bit_alu_1_cout));  // open: SET, OverFlow
  _16_bit_ALU u_16_bit_alu_2 (
    .A_16(A_32[31:16]), .LESS(1'b0), .B_16(B_32[31:16]), .Result_16(Result__32[31:16]),
    .SET(n16_bit_alu_2_set), .OverFlow(OverFlow), .AInvert(ALU_Control[3]), .BInvert(ALU_Control[2]),
    .Cin(n16_bit_alu_1_cout), .OP_2(ALU_Control[1:0]), .Cout(Cout));
  NOR_32 nor_32_1 (.OUT(ZERO), .IN(Result__32));

  // Notes on the sheet:
  //   32-bit ALU ( AND, OR, ADD, SUB, SLT, NOR )
  //   0      0    0   0
  //   AND
  //   OR
  //   ADD
  //   SUB
  //   slt
  //   NOR
  //   Ainv Binv op1 op0
  //   0      0    0   1
  //   0      0    1   0
  //   0      1    1   0
  //   0      1    1   1
  //   1      1    0   0
endmodule

module NOR_32 (
  input  [31:0] IN,
  output OUT
);

  nor nor_1 (OUT, IN[0], IN[1], IN[2], IN[3], IN[4], IN[5], IN[6], IN[7], IN[8], IN[9], IN[10], IN[11], IN[12], IN[13], IN[14], IN[15], IN[16], IN[17], IN[18], IN[19], IN[20], IN[21], IN[22], IN[23], IN[24], IN[25], IN[26], IN[27], IN[28], IN[29], IN[30], IN[31]);
endmodule

module reg_32 (
  input  [31:0] Data_32,
  input  Write,
  output [31:0] Result_32
);

  wire clock_1_out;

  Register #(.width(32)) register_1 (.D(Data_32), .en(Write), .Q(Result_32), .clk(clock_1_out));  // open: clr
  Clock clock_1 (.out(clock_1_out));
endmodule

module reg_file__32 (
  input  Write,
  input  [4:0] Read_Register_1,
  input  [4:0] Read_Register_2,
  input  [4:0] Write_Register,
  input  [31:0] DATA__32,
  output [31:0] Read_Data_1,
  output [31:0] Read_Data_2
);

  wire and_1_out, and_2_out, and_3_out, and_4_out, and_5_out, and_6_out, and_7_out, and_8_out, and_9_out,
       and_10_out, and_11_out, and_12_out, and_13_out, and_14_out, and_15_out, and_16_out, and_17_out,
       and_18_out, and_19_out, and_20_out, and_21_out, and_22_out, and_23_out, and_24_out, and_25_out,
       and_26_out, and_27_out, and_28_out, and_29_out, and_30_out, and_31_out, and_32_out, R0, R1, R2, R3,
       R4, R5, R6, R7, R8, R9, R10, R11, R12, R13, R14, R15, R16, R17, R18, R19, R20, R21, R22, R23, R24,
       R25, R26, R27, R28, R29, R30, R31;
  wire [31:0] D0, D1, D2, D3, D4, D5, D6, D7, D8, D9, D10, D11, D12, D13, D14, D15, D16, D17, D18, D19, D20,
       D21, D22, D23, D24, D25, D26, D27, D28, D29, D30, D31;

  Decoder #(.select(5)) decoder_1 (
    .out0(R0), .out1(R1), .out2(R2), .out3(R3), .out4(R4), .out5(R5), .out6(R6), .out7(R7), .out8(R8),
    .out9(R9), .out10(R10), .out11(R11), .out12(R12), .out13(R13), .out14(R14), .out15(R15), .out16(R16),
    .out17(R17), .out18(R18), .out19(R19), .out20(R20), .out21(R21), .out22(R22), .out23(R23), .out24(R24),
    .out25(R25), .out26(R26), .out27(R27), .out28(R28), .out29(R29), .out30(R30), .out31(R31),
    .sel(Write_Register));  // open: en
  and and_1 (and_1_out, Write, R0);
  and and_2 (and_2_out, Write, R1);
  and and_3 (and_3_out, Write, R2);
  and and_4 (and_4_out, Write, R3);
  and and_5 (and_5_out, Write, R4);
  and and_6 (and_6_out, Write, R5);
  and and_7 (and_7_out, Write, R6);
  and and_8 (and_8_out, Write, R7);
  and and_9 (and_9_out, Write, R8);
  and and_10 (and_10_out, Write, R9);
  and and_11 (and_11_out, Write, R10);
  and and_12 (and_12_out, Write, R11);
  and and_13 (and_13_out, Write, R12);
  and and_14 (and_14_out, Write, R13);
  and and_15 (and_15_out, Write, R14);
  and and_16 (and_16_out, Write, R15);
  reg_32 reg_32_1 (.Data_32(DATA__32), .Write(and_1_out), .Result_32(D0));
  reg_32 reg_32_2 (.Data_32(DATA__32), .Write(and_2_out), .Result_32(D1));
  reg_32 reg_32_3 (.Data_32(DATA__32), .Write(and_3_out), .Result_32(D2));
  reg_32 reg_32_4 (.Data_32(DATA__32), .Write(and_4_out), .Result_32(D3));
  reg_32 reg_32_5 (.Data_32(DATA__32), .Write(and_5_out), .Result_32(D4));
  reg_32 reg_32_6 (.Data_32(DATA__32), .Write(and_6_out), .Result_32(D5));
  reg_32 reg_32_7 (.Data_32(DATA__32), .Write(and_7_out), .Result_32(D6));
  reg_32 reg_32_8 (.Data_32(DATA__32), .Write(and_8_out), .Result_32(D7));
  reg_32 reg_32_9 (.Data_32(DATA__32), .Write(and_9_out), .Result_32(D8));
  reg_32 reg_32_10 (.Data_32(DATA__32), .Write(and_10_out), .Result_32(D9));
  reg_32 reg_32_11 (.Data_32(DATA__32), .Write(and_11_out), .Result_32(D10));
  reg_32 reg_32_12 (.Data_32(DATA__32), .Write(and_12_out), .Result_32(D11));
  reg_32 reg_32_13 (.Data_32(DATA__32), .Write(and_13_out), .Result_32(D12));
  reg_32 reg_32_14 (.Data_32(DATA__32), .Write(and_14_out), .Result_32(D13));
  reg_32 reg_32_15 (.Data_32(DATA__32), .Write(and_15_out), .Result_32(D14));
  reg_32 reg_32_16 (.Data_32(DATA__32), .Write(and_16_out), .Result_32(D15));
  and and_17 (and_17_out, Write, R16);
  and and_18 (and_18_out, Write, R17);
  and and_19 (and_19_out, Write, R18);
  and and_20 (and_20_out, Write, R19);
  and and_21 (and_21_out, Write, R20);
  and and_22 (and_22_out, Write, R21);
  and and_23 (and_23_out, Write, R22);
  and and_24 (and_24_out, Write, R23);
  and and_25 (and_25_out, Write, R24);
  and and_26 (and_26_out, Write, R25);
  and and_27 (and_27_out, Write, R26);
  and and_28 (and_28_out, Write, R27);
  and and_29 (and_29_out, Write, R28);
  and and_30 (and_30_out, Write, R29);
  and and_31 (and_31_out, Write, R30);
  and and_32 (and_32_out, Write, R31);
  reg_32 reg_32_17 (.Data_32(DATA__32), .Write(and_17_out), .Result_32(D16));
  reg_32 reg_32_18 (.Data_32(DATA__32), .Write(and_18_out), .Result_32(D17));
  reg_32 reg_32_19 (.Data_32(DATA__32), .Write(and_19_out), .Result_32(D18));
  reg_32 reg_32_20 (.Data_32(DATA__32), .Write(and_20_out), .Result_32(D19));
  reg_32 reg_32_21 (.Data_32(DATA__32), .Write(and_21_out), .Result_32(D20));
  reg_32 reg_32_22 (.Data_32(DATA__32), .Write(and_22_out), .Result_32(D21));
  reg_32 reg_32_23 (.Data_32(DATA__32), .Write(and_23_out), .Result_32(D22));
  reg_32 reg_32_24 (.Data_32(DATA__32), .Write(and_24_out), .Result_32(D23));
  reg_32 reg_32_25 (.Data_32(DATA__32), .Write(and_25_out), .Result_32(D24));
  reg_32 reg_32_26 (.Data_32(DATA__32), .Write(and_26_out), .Result_32(D25));
  reg_32 reg_32_27 (.Data_32(DATA__32), .Write(and_27_out), .Result_32(D26));
  reg_32 reg_32_28 (.Data_32(DATA__32), .Write(and_28_out), .Result_32(D27));
  reg_32 reg_32_29 (.Data_32(DATA__32), .Write(and_29_out), .Result_32(D28));
  reg_32 reg_32_30 (.Data_32(DATA__32), .Write(and_30_out), .Result_32(D29));
  reg_32 reg_32_31 (.Data_32(DATA__32), .Write(and_31_out), .Result_32(D30));
  reg_32 reg_32_32 (.Data_32(DATA__32), .Write(and_32_out), .Result_32(D31));
  Multiplexer #(.select(5), .width(32)) multiplexer_1 (
    .in0(D0), .in1(D1), .in2(D2), .in3(D3), .in4(D4), .in5(D5), .in6(D6), .in7(D7), .in8(D8), .in9(D9),
    .in10(D10), .in11(D11), .in12(D12), .in13(D13), .in14(D14), .in15(D15), .in16(D16), .in17(D17),
    .in18(D18), .in19(D19), .in20(D20), .in21(D21), .in22(D22), .in23(D23), .in24(D24), .in25(D25),
    .in26(D26), .in27(D27), .in28(D28), .in29(D29), .in30(D30), .in31(D31), .out(Read_Data_1),
    .sel(Read_Register_1));  // open: en
  Multiplexer #(.select(5), .width(32)) multiplexer_2 (
    .in0(D0), .in1(D1), .in2(D2), .in3(D3), .in4(D4), .in5(D5), .in6(D6), .in7(D7), .in8(D8), .in9(D9),
    .in10(D10), .in11(D11), .in12(D12), .in13(D13), .in14(D14), .in15(D15), .in16(D16), .in17(D17),
    .in18(D18), .in19(D19), .in20(D20), .in21(D21), .in22(D22), .in23(D23), .in24(D24), .in25(D25),
    .in26(D26), .in27(D27), .in28(D28), .in29(D29), .in30(D30), .in31(D31), .out(Read_Data_2),
    .sel(Read_Register_2));  // open: en

  // Other names for the same wires on the sheet: Data[31:0] = DATA__32; RD1[31:0] = Read_Data_1;
  //   RD2[31:0] = Read_Data_2; W = Write
endmodule

module reg_32_f (
  input  Write,
  input  [4:0] Read_data_1,
  input  [4:0] Read_data_2,
  input  [4:0] Write_Register,
  input  [31:0] DATA__32,
  output [31:0] Read_Register_1,
  output [31:0] Read_Register_2
);

  reg_file__32 reg_file_32_1 (
    .Write(Write), .Write_Register(Write_Register), .DATA__32(DATA__32), .Read_Data_1(Read_Register_1),
    .Read_Data_2(Read_Register_2), .Read_Register_1(Read_data_1), .Read_Register_2(Read_data_2));
endmodule

module left_shift_2 (
  input  [31:0] DATA__32,
  output [31:0] DATA__32_2
);


  assign DATA__32_2 = {DATA__32[29:0], 2'b00};

  // Notes on the sheet:
  //   Shift Left 2
endmodule

module sign_extension (
  input  [15:0] DATA__16,
  output [31:0] DATA__32
);


  assign DATA__32 = {{17{DATA__16[15]}}, DATA__16[14:0]};

  // Notes on the sheet:
  //   Sign Extension
endmodule

module Data_Memory (
  input  [4:0] Address_5,
  input  [31:0] Write_Data_32,
  input  Memory_Read,
  input  Memory_Write,
  output [31:0] Read_Data_32
);

  wire clock_1_out;

  Clock clock_1 (.out(clock_1_out));
  RAM #(.addrWidth(5), .dataWidth(32), .bus("separate")) ram_1 (
    .addr(Address_5), .din(Write_Data_32), .data(Read_Data_32), .str(Memory_Write), .clk(clock_1_out),
    .ld(Memory_Read));  // open: sel, clr

  // Notes on the sheet:
  //   Data Memory
endmodule

module PC_Register (
  input  [31:0] DATA_IN__32,
  output [31:0] DATA_OUT__320
);

  wire clock_1_out;

  Clock clock_1 (.out(clock_1_out));
  Register #(.width(32)) register_1 (.D(DATA_IN__32), .Q(DATA_OUT__320), .clk(clock_1_out));  // open: en, clr

  // Notes on the sheet:
  //   PC Register
endmodule

module Memory_Address (
  input  [31:0] IN_32,
  output [4:0] OUT_5
);


  assign OUT_5 = IN_32[6:2];

  // Notes on the sheet:
  //   Memory Addresss
endmodule

module ALU_Control (
  input  [1:0] ALUOp_2,
  input  [5:0] Function_6,
  output [3:0] ALUCtrl_4
);

  wire and_1_out, and_2_out, and_3_out, not_1_out;

  not not_1 (not_1_out, ALUOp_2[0]);
  and and_1 (and_1_out, ALUOp_2[1], Function_6[1]);
  nand nand_1 (ALUCtrl_4[1], ALUOp_2[1], Function_6[2]);
  and and_2 (and_2_out, ALUOp_2[1], Function_6[0]);
  and and_3 (and_3_out, ALUOp_2[1], Function_6[3]);
  or or_1 (ALUCtrl_4[2], ALUOp_2[0], and_1_out);
  or or_2 (ALUCtrl_4[0], and_2_out, and_3_out);
  and and_4 (ALUCtrl_4[3], ALUOp_2[0], not_1_out);

  // Notes on the sheet:
  //   ALU Control
  //   BNegate
  //   Op1
  //   Op0
endmodule

module Main_Control (
  input  [5:0] Opcode__6,
  output RegDest,
  output ALUSrc,
  output MemToReg,
  output RegWrite,
  output Mem_Read,
  output Mem_Write,
  output Branch,
  output ALUOp1,
  output ALUOp0
);

  and and_1 (ALUOp1, ~Opcode__6[5], ~Opcode__6[4], ~Opcode__6[3], ~Opcode__6[2], ~Opcode__6[1], ~Opcode__6[0]);  // AND_Gate
  and and_2 (Mem_Read, Opcode__6[5], ~Opcode__6[4], ~Opcode__6[3], ~Opcode__6[2], Opcode__6[1], Opcode__6[0]);  // AND_Gate
  and and_3 (Mem_Write, Opcode__6[5], ~Opcode__6[4], Opcode__6[3], ~Opcode__6[2], Opcode__6[1], Opcode__6[0]);  // AND_Gate
  and and_4 (ALUOp0, ~Opcode__6[5], ~Opcode__6[4], ~Opcode__6[3], Opcode__6[2], ~Opcode__6[1], ~Opcode__6[0]);  // AND_Gate
  or or_1 (ALUSrc, Mem_Read, Mem_Write);
  or or_2 (RegWrite, ALUOp1, Mem_Read);

  assign Branch = ALUOp0;
  assign MemToReg = Mem_Read;
  assign RegDest = ALUOp1;

  // Notes on the sheet:
  //   Main-Control-Unit
endmodule
